# Fritzing sketch Generator_Voltage_ESP8266 (saved by Fritzing 0.9.3b)
breadboards: 1

parts:
  U1 = ESP8266 NodeMCU LoLin module
  S1 = Momentary Switch [package=ksa_sealed_tac_switch]
  LED1 = smd LED [color="Red (633nm)" package="0603 [SMD]"]
  LED2 = smd LED [color="Red (633nm)" package="0603 [SMD]"]
  R1 = Resistor [tolerance=±5% resistance=220 package="2512 [SMD]"]
  R2 = Resistor [tolerance=±5% resistance=220 package="2512 [SMD]"]
  Power_plug1 = Power plug

nets:
  N1: U1.D3, S1.2
  N2: U1.GND, S1.3, LED1.cathode, LED2.cathode
  N3: U1.D5, R1.Pin_1
  N4: U1.D6, R2.Pin_1
  N5: U1.A0, Power_plug1.VCC
  N6: LED1.anode, R2.Pin_0
  N7: LED2.anode, R1.Pin_0

custom parts:
  ESP8266 NodeMCU LoLin module: ESP8266 based NodeMCU
