# Fritzing sketch WeatherStation (saved by Fritzing 0.9.3b)
breadboards: 1

parts:
  U1 = ESP8266 NodeMCU LoLin module
  OLED1 = OLED 128x64 I2C Monochrome Display GND-VDD
  S1 = Momentary Switch [package=ksa_sealed_tac_switch]
  LED1 = smd LED [color="Red (633nm)" package="0603 [SMD]"]
  LED2 = smd LED [color="Red (633nm)" package="0603 [SMD]"]
  R1 = Resistor [tolerance=±5% resistance=220 package="2512 [SMD]"]
  R2 = Resistor [tolerance=±5% resistance=220 package="2512 [SMD]"]
  A1 = DHT22 module

nets:
  N1: U1.D1, OLED1.SDA
  N2: U1.D2, OLED1.SCK
  N3: U1.D3, S1.2
  3V3: U1.3V3, OLED1.VDD, A1.+
  GND: U1.GND, OLED1.GND, S1.3, LED1.cathode, LED2.cathode, A1.-
  N4: U1.D5, R1.Pin_1
  N5: U1.D6, R2.Pin_1
  N6: U1.D7, A1.Out
  N7: LED1.anode, R2.Pin_0
  N8: LED2.anode, R1.Pin_0

custom parts:
  ESP8266 NodeMCU LoLin module: ESP8266 based NodeMCU
  OLED 128x64 I2C Monochrome Display GND-VDD: OLED 128x64 I2C Monochrome Display. Note: there are two variants of this part, this one is the GND VDD SCK SDA variant. The other is VDD GND SCK SDA. Make sure you select the part that matches your module as using the incorrect part will probably destroy your module! In addition the mounting holes are marked on silkscreen but not by default drilled. If you want drilled mounting holes, copy a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
  DHT22 module: DHT22 module. Pins VCC Data GND.
